# Fritzing sketch Rangkaian Disinfektan (saved by Fritzing 0.9.2b)
breadboards: 1

parts:
  Part1 = Arduino Nano (Rev3.0)
  M1 = E18-D80NK_1 [package=THT]
  U1 = 2-Channel 5v Relay Shield [package=relay-2ch5v10a]

nets:
  GND: Part1.GND, M1.pin2, U1.GND
  N1: Part1.D2, M1.pin3
  N2: Part1.D4, U1.IN2
  N3: Part1.D5, U1.IN1
  5V: Part1.5V, M1.pin1, U1.VCC

custom parts:
  E18-D80NK_1: E18-D80NK Proximity Sensor module.
  2-Channel 5v Relay Shield: 2 Channel 5v Relay Shield w. 2x SPD-06VDC-SD-C
